// Logisim project logisim.circ as structural Verilog: 1 circuit, main circuit main
module main (
  input  H,
  output p,
  output l
);

  wire and_1_out, and_2_out, and_3_out, and_4_out, clock_1_out, d_ff_2_qn, not_1_out, not_2_out, or_1_out,
       or_2_out;

  not not_1 (not_1_out, H);
  not not_2 (not_2_out, H);
  and and_1 (and_1_out, p, not_1_out);
  and and_2 (and_2_out, d_ff_2_qn, H);
  and and_3 (and_3_out, l, not_2_out);
  and and_4 (and_4_out, p, H);
  Clock clock_1 (.out(clock_1_out));
  D_Flip_Flop d_ff_1 (.D(or_1_out), .clk(clock_1_out), .Q(p));  // open: Qn, preset, reset
  or or_1 (or_1_out, and_1_out, and_2_out);
  D_Flip_Flop d_ff_2 (.D(or_2_out), .clk(clock_1_out), .Q(l), .Qn(d_ff_2_qn));  // open: preset, reset
  or or_2 (or_2_out, and_3_out, and_4_out);
endmodule
