// Logisim project Diagrama_de_Circuitos.circ as structural Verilog: 1 circuit, main circuit main
module main (
  input  x,
  input  y,
  input  z,
  output F
);

  wire and_1_out, and_2_out, not_1_out, not_2_out;

  not not_1 (not_1_out, y);
  not not_2 (not_2_out, x);
  and and_1 (and_1_out, x, not_1_out);
  or or_1 (F, and_1_out, and_2_out);
  and and_2 (and_2_out, not_2_out, z);
endmodule
