// Logisim project DiagramaDeCircuitos5.circ as structural Verilog: 1 circuit, main circuit Motores_p5
module Motores_p5 (
  input  C1,
  input  C2,
  input  C3,
  input  C4,
  output M1,
  output M2,
  output M3,
  output M4
);

  wire and_1_out, and_2_out, and_3_out, and_4_out, and_5_out, not_1_out, not_2_out, not_3_out;

  not not_1 (not_1_out, C1);
  not not_2 (not_2_out, C2);
  not not_3 (not_3_out, C3);
  and and_1 (and_1_out, not_1_out, C3);
  and and_2 (and_2_out, not_2_out, C3);
  and and_3 (and_3_out, not_1_out, not_2_out, C4);
  and and_4 (and_4_out, not_1_out, not_3_out, C4);
  and and_5 (and_5_out, not_2_out, not_3_out, C4);
  or or_1 (M3, and_1_out, and_2_out);
  or or_2 (M4, and_3_out, and_4_out, and_5_out);

  assign M1 = C1;
  assign M2 = C2;
endmodule
